# Fritzing sketch schematic (saved by Fritzing 1.0.5)

parts:
  MCU1 = Raspberry Pi Zero
  Q1 = TIP120 Hi-Current Darlington Transistor
  Q2 = TIP120 Hi-Current Darlington Transistor
  Q3 = TIP120 Hi-Current Darlington Transistor
  A1 = RGB Strip LED
  Power_plug1 = Power plug

nets:
  N1: MCU1.pin_6, MCU1.pin_9, MCU1.pin_25, MCU1.pin_39, Q1.EMITTER, Q2.EMITTER, Q3.EMITTER, Power_plug1.GND
  N2: MCU1.pin_11, Q1.BASE
  N3: MCU1.pin_13, Q2.BASE
  N4: MCU1.pin_15, Q3.BASE
  N5: Q1.COLLECTOR, A1.Green_Connect
  N6: Q2.COLLECTOR, A1.Red_Connect
  N7: Q3.COLLECTOR, A1.Blue_Connect
  N8: A1.Common_Connect, Power_plug1.VCC

custom parts:
  RGB Strip LED: A tri-color Strip LED with red, green and blue. Pin order: red - common cathode - blue - green
